# Fritzing sketch schematic_fritzing (saved by Fritzing 0.9.3b)

parts:
  Part1 = Adafruit Flora [part_number="Adafruit #659"]
  Part3 = RFID-RC522-v2
  JACK1 = 2.1mm Barrel Jack with Terminal Block
  Part2 = Thermal Printer

nets:
  +3V3: Part1.+3V3, Part3.3.3V
  N1: Part1.IO6, Part2.TXD
  GND: Part1.GND, Part3.GND, Part2.GND#2
  N2: Part1.IO9, Part3.RST
  N3: Part1.IO10, Part3.NSS
  N4: Part1.MISO, Part3.MISO
  N5: Part1.SCK, Part3.SCK
  N6: Part1.MOSI, Part3.MOSI
  N7: JACK1.POS, Part2.VH
  N8: JACK1.NEG, Part2.GND#0

custom parts:
  Adafruit Flora: FLORA is Adafruit's fully-featured wearable electronics platform. It's a round, sewable, Arduino-compatible microcontroller designed to empower amazing wearables projects. The FLORA is small (1.75" diameter, weighing 4.4 grams). The FLORA has built-in USB support. Built in USB means you plug it in to program it, it just shows up - all you need is a Micro-B USB cable, no additional purchases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
  RFID-RC522-v2: A simple China made RFID-RC522 Reader; do check the pin labels, as this is a MFRC522 based clone.
